# Fritzing sketch AntiBueeNano2 (saved by Fritzing 0.9.3b)
stripboards: 1

parts:
  R2 = Resistor [tolerance=±5% resistance=1k package="0805 [SMD]"]
  Composant3 = Arduino Nano (Rev3.0) (ICSP)
  12V_caméra = Camdenboss CTB0158-2 [part_number=CTB0158-2 package=THT]
  MPU6050 = female pin header, 8 pins [form="♀ (female)"]
  BME280 = female pin header, 4 pins [form="♀ (female)"]
  Q2 = MOSFET-NCHANNEL [package=to220v]
  R3 = Resistor [tolerance=±5% resistance=6.8k package="0805 [SMD]"]
  Composant1 = InvenSense MPU6050  # not connected
  Alimentation_5-0-Park-12V = shrouded pin header, 8 pins [form="♂ (shrouded male)"]
  1Wire = shrouded pin header, 6 pins [form="♂ (shrouded male)"]
  LED = female pin header, 3 pins [form="♀ (female)"]
  Chauffage_(1-3) = shrouded pin header, 6 pins [form="♂ (shrouded male)"]

nets:
  N1: R2.Pin_0, Composant3.D11/MOSI, Q2.G, Chauffage_(1-3).pin2, Chauffage_(1-3).pin5
  N2: R2.Pin_1, Composant3.GND, 12V_caméra.pin1, MPU6050.pin7, BME280.pin3, Q2.S, Alimentation_5-0-Park-12V.pin2, Alimentation_5-0-Park-12V.pin7, 1Wire.pin3, 1Wire.pin4, LED.pin3
  N3: Composant3.D2, R3.Pin_1, 1Wire.pin2, 1Wire.pin5
  N4: Composant3.D3, 1Wire.pin1, 1Wire.pin6
  N5: Composant3.D9, LED.pin1
  N6: Composant3.5V, MPU6050.pin8, BME280.pin4, R3.Pin_0, Alimentation_5-0-Park-12V.pin1, Alimentation_5-0-Park-12V.pin8, LED.pin2
  N7: Composant3.A5, MPU6050.pin6, BME280.pin2
  N8: Composant3.A4, MPU6050.pin5, BME280.pin1
  N9: Composant3.A0, Alimentation_5-0-Park-12V.pin3, Alimentation_5-0-Park-12V.pin6
  N10: 12V_caméra.pin2, Alimentation_5-0-Park-12V.pin4, Alimentation_5-0-Park-12V.pin5, Chauffage_(1-3).pin3, Chauffage_(1-3).pin4
  N11: Q2.D, Chauffage_(1-3).pin1, Chauffage_(1-3).pin6
